// Logisim project 24520022_-_3.1.circ as structural Verilog: 1 circuit, main circuit main
module main (
  input  a,
  input  b,
  input  c,
  output f
);

  wire and_1_out;

  and and_1 (and_1_out, a, b);
  or or_1 (f, and_1_out, c);
endmodule
